# Fritzing sketch esp8266_mqtt_distancia (saved by Fritzing 0.9.3b)
breadboards: 1

parts:
  U1 = ESP8266 WiFi Module [part_number=ESP8266]
  hc-sr1 = hc-sr04
  Power_plug1 = Power plug
  REG1 = LD33 Low-Dropout Voltage Regulator
  R1 = Resistor [tolerance=±5% resistance=470 package=THT]

nets:
  N1: U1.VCC, REG1.Vout, R1.Pin_0
  N2: U1.GPIO_0, hc-sr1.Trig
  N3: U1.GPIO_2, hc-sr1.Echo
  N4: U1.CH_PD, R1.Pin_1
  GND: U1.GND, hc-sr1.GND, Power_plug1.GND, REG1.GND
  VCC: hc-sr1.VCC, Power_plug1.VCC, REG1.Vin

custom parts:
  ESP8266 WiFi Module: Generic WiFi Module based on the ESP8266 with onboard PCB antenna and UART communications
